// Logisim project Project.circ as structural Verilog
module main (
  input  RESET_COUNTER,
  input  A_INVERT,
  output [8:0] out_3,
  output [11:0] out_4,
  output [11:0] RD_1,
  output [11:0] RD_2,
  output [2:0] OP_CODE,
  output [2:0] RS_BASE,
  output [2:0] RT,
  output [2:0] RD,
  output ZERO,
  output OVERFLOW,
  output [11:0] out_13
);

  wire CLK_out, control_unit_1_alu_source, control_unit_1_b_invert, control_unit_1_cin, control_unit_1_jump,
       control_unit_1_load_enable, control_unit_1_ram_to_register, control_unit_1_register_destination,
       control_unit_1_store_enable, control_unit_1_write_enable;
  wire [1:0] control_unit_1_alu_operation;
  wire [2:0] multiplexer_2_out;
  wire [11:0] adder_1_out, alu_12_bit_1_result, bit_extender_1_out, multiplexer_1_out, ram_1_dout,
       register_file_12_bit_1_rd2;

  Adder #(.width(12)) adder_1 (.a(out_4), .b(12'h1), .out(adder_1_out));  // open: cin, cout
  Multiplexer #(.width(12)) multiplexer_1 (
    .in0(adder_1_out), .in1({out_4[11:9], out_3}), .out(multiplexer_1_out), .sel(control_unit_1_jump));
  Clock CLK (.out(CLK_out));
  Register #(.width(12)) register_1 (.D(multiplexer_1_out), .clk(CLK_out), .Q(out_4), .clr(RESET_COUNTER));  // open: en
  CONTROL_UNIT control_unit_1 (
    .OP_CODE(OP_CODE), .REGISTER_DESTINATION(control_unit_1_register_destination),
    .B_INVERT(control_unit_1_b_invert), .Cin(control_unit_1_cin),
    .ALU_OPERATION(control_unit_1_alu_operation), .ALU_SOURCE(control_unit_1_alu_source),
    .WRITE_ENABLE(control_unit_1_write_enable), .STORE_ENABLE(control_unit_1_store_enable),
    .LOAD_ENABLE(control_unit_1_load_enable), .RAM_TO_REGISTER(control_unit_1_ram_to_register),
    .JUMP(control_unit_1_jump));
  ROM #(.addrWidth(12), .dataWidth(12)) rom_1 (.addr(out_4), .data({OP_CODE, out_3}));
  Multiplexer #(.width(3)) multiplexer_2 (
    .in0(out_3[2:0]), .in1(out_3[5:3]), .out(multiplexer_2_out), .sel(control_unit_1_register_destination));
  assign bit_extender_1_out = {{9{1'b0}}, out_3[2:0]};  // Bit_Extender bit_extender_1
  Register_File_12_bit register_file_12_bit_1 (
    .RD1(RD_1), .RD2(register_file_12_bit_1_rd2), .WE(control_unit_1_write_enable), .CLK(CLK_out),
    .WR(multiplexer_2_out), .WD(out_13), .RR1(out_3[8:6]), .RR2(out_3[5:3]));  // open: Reset
  Multiplexer #(.width(12)) multiplexer_3 (
    .in0(register_file_12_bit_1_rd2), .in1(bit_extender_1_out), .out(RD_2), .sel(control_unit_1_alu_source));
  ALU_12_BIT alu_12_bit_1 (
    .OVERFLOW(OVERFLOW), .ZERO(ZERO), .RESULT(alu_12_bit_1_result), .A_inv(A_INVERT),
    .B_inv(control_unit_1_b_invert), .OP_CODE(control_unit_1_alu_operation), .Cin(control_unit_1_cin),
    .A(RD_1), .B(RD_2));
  RAM #(.addrWidth(12), .asyncread("true"), .clearpin("true"), .dataWidth(12)) ram_1 (
    .addr(alu_12_bit_1_result), .we(control_unit_1_store_enable), .oe(control_unit_1_load_enable),
    .clk(CLK_out), .din(register_file_12_bit_1_rd2), .dout(ram_1_dout));  // open: clr
  Multiplexer #(.width(12)) multiplexer_4 (
    .in0(alu_12_bit_1_result), .in1(ram_1_dout), .out(out_13), .sel(control_unit_1_ram_to_register));

  assign RD = out_3[2:0];
  assign RS_BASE = out_3[8:6];
  assign RT = out_3[5:3];

  // Notes on the sheet:
  //   contents of rom_1 (hex, n*v repeats v):
  //   50e 794
endmodule

module ALU_1_BIT (
  input  Cin,
  input  A,
  input  B,
  input  A_inv,
  input  B_inv,
  input  [1:0] Op,
  output Result,
  output Cout
);

  wire and_1_out, full_adder_1_bit_1_sum, multiplexer_1_out, multiplexer_2_out, not_1_out, not_2_out,
       or_1_out;

  Multiplexer multiplexer_1 (.in0(A), .in1(not_1_out), .out(multiplexer_1_out), .sel(A_inv));
  not not_1 (not_1_out, A);
  not not_2 (not_2_out, B);
  Multiplexer multiplexer_2 (.in0(B), .in1(not_2_out), .out(multiplexer_2_out), .sel(B_inv));
  FULL_ADDER_1_BIT full_adder_1_bit_1 (
    .SUM(full_adder_1_bit_1_sum), .Cout(Cout), .Ib(multiplexer_2_out), .Cin(Cin), .Ia(multiplexer_1_out));
  and and_1 (and_1_out, multiplexer_1_out, multiplexer_2_out);
  or or_1 (or_1_out, multiplexer_1_out, multiplexer_2_out);
  Info info_1 ();
  MUX_4x1 mux_4x1_1 (
    .Y(Result), .S1(Op[1]), .S0(Op[0]), .D2(full_adder_1_bit_1_sum), .D1(or_1_out), .D0(and_1_out));  // open: D3, E0
endmodule

module ALU_12_BIT (
  input  Cin,
  input  [11:0] A,
  input  [11:0] B,
  input  A_inv,
  input  B_inv,
  input  [1:0] OP_CODE,
  output ZERO,
  output [11:0] RESULT,
  output OVERFLOW
);

  wire ALU_0_cout, ALU_1_cout, ALU_2_cout, ALU_3_cout, ALU_4_cout, ALU_5_cout, ALU_6_cout, ALU_7_cout,
       ALU_8_cout, ALU_9_cout, ALU_10_cout;

  ALU_1_BIT ALU_0 (
    .Result(RESULT[0]), .Cout(ALU_0_cout), .A(A[0]), .B(B[0]), .A_inv(A_inv), .B_inv(B_inv), .Cin(Cin),
    .Op(OP_CODE));
  ALU_1_BIT ALU_1 (
    .Result(RESULT[1]), .Cout(ALU_1_cout), .A(A[1]), .B(B[1]), .A_inv(A_inv), .B_inv(B_inv),
    .Cin(ALU_0_cout), .Op(OP_CODE));
  ALU_1_BIT ALU_2 (
    .Result(RESULT[2]), .Cout(ALU_2_cout), .A(A[2]), .B(B[2]), .A_inv(A_inv), .B_inv(B_inv),
    .Cin(ALU_1_cout), .Op(OP_CODE));
  ALU_1_BIT ALU_3 (
    .Result(RESULT[3]), .Cout(ALU_3_cout), .A(A[3]), .B(B[3]), .A_inv(A_inv), .B_inv(B_inv),
    .Cin(ALU_2_cout), .Op(OP_CODE));
  ALU_1_BIT ALU_4 (
    .Result(RESULT[4]), .Cout(ALU_4_cout), .A(A[4]), .B(B[4]), .A_inv(A_inv), .B_inv(B_inv),
    .Cin(ALU_3_cout), .Op(OP_CODE));
  ALU_1_BIT ALU_5 (
    .Result(RESULT[5]), .Cout(ALU_5_cout), .A(A[5]), .B(B[5]), .A_inv(A_inv), .B_inv(B_inv),
    .Cin(ALU_4_cout), .Op(OP_CODE));
  ALU_1_BIT ALU_6 (
    .Result(RESULT[6]), .Cout(ALU_6_cout), .A(A[6]), .B(B[6]), .A_inv(A_inv), .B_inv(B_inv),
    .Cin(ALU_5_cout), .Op(OP_CODE));
  ALU_1_BIT ALU_7 (
    .Result(RESULT[7]), .Cout(ALU_7_cout), .A(A[7]), .B(B[7]), .A_inv(A_inv), .B_inv(B_inv),
    .Cin(ALU_6_cout), .Op(OP_CODE));
  ALU_1_BIT ALU_8 (
    .Result(RESULT[8]), .Cout(ALU_8_cout), .A(A[8]), .B(B[8]), .A_inv(A_inv), .B_inv(B_inv),
    .Cin(ALU_7_cout), .Op(OP_CODE));
  ALU_1_BIT ALU_9 (
    .Result(RESULT[9]), .Cout(ALU_9_cout), .A(A[9]), .B(B[9]), .A_inv(A_inv), .B_inv(B_inv),
    .Cin(ALU_8_cout), .Op(OP_CODE));
  ALU_1_BIT ALU_10 (
    .Result(RESULT[10]), .Cout(ALU_10_cout), .A(A[10]), .B(B[10]), .A_inv(A_inv), .B_inv(B_inv),
    .Cin(ALU_9_cout), .Op(OP_CODE));
  ALU_1_BIT ALU_11 (
    .Result(RESULT[11]), .Cout(OVERFLOW), .A(A[11]), .B(B[11]), .A_inv(A_inv), .B_inv(B_inv),
    .Cin(ALU_10_cout), .Op(OP_CODE));
  nor nor_1 (ZERO, RESULT[0], RESULT[1], RESULT[2], RESULT[3], RESULT[4], RESULT[5], RESULT[7], RESULT[8], RESULT[9], RESULT[10], RESULT[11], RESULT[6]);
endmodule

module D_FLIP_FLOP (
  input  Set,
  input  Clock,
  input  Data,
  input  Reset,
  output Q,
  output Q_not
);

  wire nand_1_out, nand_2_out, nand_3_out, nand_4_out, not_1_out, not_2_out;

  not not_1 (not_1_out, Set);
  not not_2 (not_2_out, Reset);
  nand nand_1 (nand_1_out, not_1_out, nand_4_out, nand_2_out);
  nand nand_2 (nand_2_out, nand_1_out, Clock, not_2_out);
  nand nand_3 (nand_3_out, nand_2_out, Clock, nand_4_out);
  nand nand_4 (nand_4_out, nand_3_out, Data, not_2_out);
  nand nand_5 (Q, not_1_out, nand_2_out, Q_not);
  nand nand_6 (Q_not, Q, nand_3_out, not_2_out);
endmodule

module FULL_ADDER_1_BIT (
  input  Ia,
  input  Ib,
  input  Cin,
  output SUM,
  output Cout
);

  wire and_1_out, and_2_out, xor_1_out;

  xor xor_1 (xor_1_out, Ia, Ib);
  and and_1 (and_1_out, Ia, Ib);
  xor xor_2 (SUM, xor_1_out, Cin);
  and and_2 (and_2_out, xor_1_out, Cin);
  or or_1 (Cout, and_2_out, and_1_out);
endmodule

module IC_7486_XOR (
  input  A1,
  input  B1,
  input  A2,
  input  B2,
  input  A3,
  input  B3,
  input  A4,
  input  B4,
  output O1,
  output O2,
  output O3,
  output O4
);

  xor xor_1 (O1, A1, B1);
  xor xor_2 (O2, A2, B2);
  xor xor_3 (O3, A3, B3);
  xor xor_4 (O4, A4, B4);
endmodule

module MUX_4x1 (
  input  E0,
  input  S1,
  input  S0,
  input  D3,
  input  D2,
  input  D1,
  input  D0,
  output Y
);

  wire and_1_out, and_2_out, and_3_out, and_4_out, not_1_out, not_2_out, not_3_out;

  not not_1 (not_1_out, E0);
  not not_2 (not_2_out, S1);
  not not_3 (not_3_out, S0);
  and and_1 (and_1_out, D0, not_3_out, not_2_out, not_1_out);
  and and_2 (and_2_out, D1, S0, not_2_out, not_1_out);
  and and_3 (and_3_out, D2, not_3_out, S1, not_1_out);
  and and_4 (and_4_out, D3, S0, S1, not_1_out);
  or or_1 (Y, and_1_out, and_2_out, and_3_out, and_4_out);
endmodule

module Register_File_12_bit (
  input  [2:0] RR1,
  input  [11:0] WD,
  input  Reset,
  input  [2:0] RR2,
  input  WE,
  input  [2:0] WR,
  input  CLK,
  output [11:0] RD1,
  output [11:0] RD2
);

  wire decoder_1_out0, decoder_1_out1, decoder_1_out2, decoder_1_out3, decoder_1_out4, decoder_1_out5,
       decoder_1_out6, decoder_1_out7;
  wire [11:0] REG_0_q, REG_1_q, REG_2_q, REG_3_q, REG_4_q, REG_5_q, REG_6_q, REG_7_q;

  Decoder #(.select(3)) decoder_1 (
    .out0(decoder_1_out0), .out1(decoder_1_out1), .out2(decoder_1_out2), .out3(decoder_1_out3),
    .out4(decoder_1_out4), .out5(decoder_1_out5), .out6(decoder_1_out6), .out7(decoder_1_out7), .sel(WR),
    .en(WE));
  Register #(.width(12)) REG_0 (.D(WD), .en(decoder_1_out0), .clk(CLK), .Q(REG_0_q), .clr(Reset));
  Register #(.width(12)) REG_1 (.D(WD), .en(decoder_1_out1), .clk(CLK), .Q(REG_1_q), .clr(Reset));
  Register #(.width(12)) REG_2 (.D(WD), .en(decoder_1_out2), .clk(CLK), .Q(REG_2_q), .clr(Reset));
  Register #(.width(12)) REG_3 (.D(WD), .en(decoder_1_out3), .clk(CLK), .Q(REG_3_q), .clr(Reset));
  Register #(.width(12)) REG_4 (.D(WD), .en(decoder_1_out4), .clk(CLK), .Q(REG_4_q), .clr(Reset));
  Register #(.width(12)) REG_5 (.D(WD), .en(decoder_1_out5), .clk(CLK), .Q(REG_5_q), .clr(Reset));
  Register #(.width(12)) REG_6 (.D(WD), .en(decoder_1_out6), .clk(CLK), .Q(REG_6_q), .clr(Reset));
  Register #(.width(12)) REG_7 (.D(WD), .en(decoder_1_out7), .clk(CLK), .Q(REG_7_q), .clr(Reset));
  Multiplexer #(.select(3), .width(12)) multiplexer_1 (
    .in0(REG_0_q), .in1(REG_1_q), .in2(REG_2_q), .in3(REG_3_q), .in4(REG_4_q), .in5(REG_5_q), .in6(REG_6_q),
    .in7(REG_7_q), .out(RD1), .sel(RR1));
  Multiplexer #(.select(3), .width(12)) multiplexer_2 (
    .in0(REG_0_q), .in1(REG_1_q), .in2(REG_2_q), .in3(REG_3_q), .in4(REG_4_q), .in5(REG_5_q), .in6(REG_6_q),
    .in7(REG_7_q), .out(RD2), .sel(RR2));
endmodule

module test (
  input  RESET_COUNTER,
  input  A_INVERT,
  output [8:0] out_3,
  output [11:0] out_4,
  output [11:0] RD_1,
  output [11:0] RD_2,
  output [2:0] OP_CODE,
  output [2:0] RS_BASE,
  output [2:0] RT,
  output [2:0] RD,
  output ZERO,
  output OVERFLOW,
  output [11:0] out_13
);

  wire CLK_out, control_unit_1_alu_source, control_unit_1_b_invert, control_unit_1_cin, control_unit_1_jump,
       control_unit_1_load_enable, control_unit_1_ram_to_register, control_unit_1_register_destination,
       control_unit_1_store_enable, control_unit_1_write_enable;
  wire [1:0] control_unit_1_alu_operation;
  wire [2:0] multiplexer_2_out;
  wire [11:0] adder_1_out, alu_12_bit_1_result, bit_extender_1_out, multiplexer_1_out, ram_1_dout,
       register_file_12_bit_1_rd2;

  Adder #(.width(12)) adder_1 (.a(out_4), .b(12'h1), .out(adder_1_out));  // open: cin, cout
  Multiplexer #(.width(12)) multiplexer_1 (
    .in0(adder_1_out), .in1({out_4[11:9], out_3}), .out(multiplexer_1_out), .sel(control_unit_1_jump));
  Clock CLK (.out(CLK_out));
  Register #(.width(12)) register_1 (.D(multiplexer_1_out), .clk(CLK_out), .Q(out_4), .clr(RESET_COUNTER));  // open: en
  CONTROL_UNIT control_unit_1 (
    .OP_CODE(OP_CODE), .REGISTER_DESTINATION(control_unit_1_register_destination),
    .B_INVERT(control_unit_1_b_invert), .Cin(control_unit_1_cin),
    .ALU_OPERATION(control_unit_1_alu_operation), .ALU_SOURCE(control_unit_1_alu_source),
    .WRITE_ENABLE(control_unit_1_write_enable), .STORE_ENABLE(control_unit_1_store_enable),
    .LOAD_ENABLE(control_unit_1_load_enable), .RAM_TO_REGISTER(control_unit_1_ram_to_register),
    .JUMP(control_unit_1_jump));
  ROM #(.addrWidth(12), .dataWidth(12)) rom_1 (.addr(out_4), .data({OP_CODE, out_3}));
  Multiplexer #(.width(3)) multiplexer_2 (
    .in0(out_3[2:0]), .in1(out_3[5:3]), .out(multiplexer_2_out), .sel(control_unit_1_register_destination));
  assign bit_extender_1_out = {{9{out_3[2]}}, out_3[2:0]};  // Bit_Extender bit_extender_1
  Register_File_12_bit register_file_12_bit_1 (
    .RD1(RD_1), .RD2(register_file_12_bit_1_rd2), .WE(control_unit_1_write_enable), .CLK(CLK_out),
    .WR(multiplexer_2_out), .WD(out_13), .RR1(out_3[8:6]), .RR2(out_3[5:3]));  // open: Reset
  Multiplexer #(.width(12)) multiplexer_3 (
    .in0(register_file_12_bit_1_rd2), .in1(bit_extender_1_out), .out(RD_2), .sel(control_unit_1_alu_source));
  ALU_12_BIT alu_12_bit_1 (
    .OVERFLOW(OVERFLOW), .ZERO(ZERO), .RESULT(alu_12_bit_1_result), .A_inv(A_INVERT),
    .B_inv(control_unit_1_b_invert), .OP_CODE(control_unit_1_alu_operation), .Cin(control_unit_1_cin),
    .A(RD_1), .B(RD_2));
  RAM #(.addrWidth(12), .asyncread("true"), .clearpin("true"), .dataWidth(12)) ram_1 (
    .addr(alu_12_bit_1_result), .we(control_unit_1_store_enable), .oe(control_unit_1_load_enable),
    .clk(CLK_out), .din(register_file_12_bit_1_rd2), .dout(ram_1_dout));  // open: clr
  Multiplexer #(.width(12)) multiplexer_4 (
    .in0(alu_12_bit_1_result), .in1(ram_1_dout), .out(out_13), .sel(control_unit_1_ram_to_register));

  assign RD = out_3[2:0];
  assign RS_BASE = out_3[8:6];
  assign RT = out_3[5:3];

  // Notes on the sheet:
  //   contents of rom_1 (hex, n*v repeats v):
  //   12e 32c 12c c01 63*0 c01
endmodule

module CONTROL_UNIT (
  input  [2:0] OP_CODE,
  output REGISTER_DESTINATION,
  output B_INVERT,
  output Cin,
  output [1:0] ALU_OPERATION,
  output ALU_SOURCE,
  output WRITE_ENABLE,
  output STORE_ENABLE,
  output LOAD_ENABLE,
  output RAM_TO_REGISTER,
  output JUMP
);

  wire and_1_out, and_2_out, and_5_out, and_6_out, and_7_out, not_1_out, not_2_out, not_3_out;

  not not_1 (not_1_out, OP_CODE[2]);
  not not_2 (not_2_out, OP_CODE[1]);
  not not_3 (not_3_out, OP_CODE[0]);
  and and_1 (and_1_out, not_1_out, OP_CODE[1]);
  and and_2 (and_2_out, OP_CODE[2], not_2_out);
  and and_3 (B_INVERT, not_2_out, OP_CODE[0]);
  and and_4 (Cin, not_2_out, OP_CODE[0]);
  or or_1 (ALU_OPERATION[1], not_1_out, not_2_out);
  and and_5 (and_5_out, not_1_out, OP_CODE[1]);
  and and_6 (and_6_out, OP_CODE[2], not_2_out);
  and and_7 (and_7_out, not_1_out, OP_CODE[0]);
  and and_8 (STORE_ENABLE, not_1_out, OP_CODE[1], not_3_out);
  and and_9 (LOAD_ENABLE, not_1_out, OP_CODE[1], OP_CODE[0]);
  and and_10 (RAM_TO_REGISTER, not_1_out, OP_CODE[1], OP_CODE[0]);
  and and_11 (JUMP, OP_CODE[2], OP_CODE[1], not_3_out);
  or or_2 (REGISTER_DESTINATION, and_1_out, and_2_out);
  or or_3 (ALU_SOURCE, and_5_out, and_6_out);
  or or_4 (WRITE_ENABLE, not_2_out, and_7_out);

  assign ALU_OPERATION[0] = 1'b0;
endmodule
